# Fritzing sketch schematic_v0.1 (saved by Fritzing 0.9.10b)
perfboards: 2

parts:
  Part1 = Arduino Mega ADK (Rev3)
  Q1 = Basic FET N-Channel [package="D2Pak [SMD]"]
  Q2 = Basic FET N-Channel [package="D2Pak [SMD]"]
  Q3 = Basic FET N-Channel [package="D2Pak [SMD]"]
  Q4 = Basic FET N-Channel [package="D2Pak [SMD]"]
  J1 = Camdenboss CTB0158-12 [part_number=CTB0158-12 package=THT]
  M1 = RioRand LM2596
  IC1 = MICROCONTROLLER [package=dil28-3-zif_socket]  # not connected
  J2 = Camdenboss CTB0158-2 [part_number=CTB0158-2 package=THT]
  J3 = Camdenboss CTB0158-6 [part_number=CTB0158-6 package=THT]  # not connected
  J4 = Camdenboss CTB0158-2 [part_number=CTB0158-2 package=THT]
  J5 = Camdenboss CTB0158-2 [part_number=CTB0158-2 package=THT]
  J6 = Camdenboss CTB0158-2 [part_number=CTB0158-2 package=THT]
  J7 = Camdenboss CTB0158-2 [part_number=CTB0158-2 package=THT]
  J8 = Camdenboss CTB0158-2 [part_number=CTB0158-2 package=THT]
  J9 = Camdenboss CTB0158-6 [part_number=CTB0158-6 package=THT]  # not connected
  LED1 = LEDs [package=led10mm]
  LED2 = LEDs [package=led10mm]
  M3 = DC Motor [voltage_(max)=6V voltage_(min)=3V]
  LED3 = LEDs [package=led10mm]
  M4 = DC Motor [voltage_(max)=6V voltage_(min)=3V]
  LED4 = LEDs [package=led10mm]
  M5 = DC Motor [voltage_(max)=6V voltage_(min)=3V]
  J22 = Camdenboss CTB0158-6 [part_number=CTB0158-6 package=THT]
  J24 = Camdenboss CTB0158-6 [part_number=CTB0158-6 package=THT]
  J25 = Camdenboss CTB0158-6 [part_number=CTB0158-6 package=THT]
  J26 = Camdenboss CTB0158-6 [part_number=CTB0158-6 package=THT]
  J27 = Camdenboss CTB0158-6 [part_number=CTB0158-6 package=THT]
  J23 = Camdenboss CTB0158-7 [part_number=CTB0158-7 package=THT]
  J28 = Camdenboss CTB0158-12 [part_number=CTB0158-12 package=THT]
  J19 = Camdenboss CTB0158-5 [part_number=CTB0158-5 package=THT]
  J29 = Camdenboss CTB0158-5 [part_number=CTB0158-5 package=THT]
  J21 = Camdenboss CTB0158-5 [part_number=CTB0158-5 package=THT]
  J30 = Camdenboss CTB0158-5 [part_number=CTB0158-5 package=THT]
  J31 = Camdenboss CTB0158-5 [part_number=CTB0158-5 package=THT]
  J32 = Camdenboss CTB0158-5 [part_number=CTB0158-5 package=THT]
  J33 = Camdenboss CTB0158-5 [part_number=CTB0158-5 package=THT]
  J34 = Camdenboss CTB0158-5 [part_number=CTB0158-5 package=THT]
  J35 = Camdenboss CTB0158-5 [part_number=CTB0158-5 package=THT]
  J36 = Camdenboss CTB0158-5 [part_number=CTB0158-5 package=THT]
  J37 = Camdenboss CTB0158-5 [part_number=CTB0158-5 package=THT]
  J38 = Camdenboss CTB0158-5 [part_number=CTB0158-5 package=THT]
  J39 = female pin header, 14 pins [form="♀ (female)"]
  J40 = female pin header, 14 pins [form="♀ (female)"]
  M2 = DC Motor [voltage_(max)=6V voltage_(min)=3V]
  J41 = Camdenboss CTB0158-5 [part_number=CTB0158-5 package=THT]
  R1 = Resistor [tolerance=±5% power=0.25 resistance=10k package=THT]
  R2 = Resistor [tolerance=±5% power=0.25 resistance=10k package=THT]
  R3 = Resistor [tolerance=±5% power=0.25 resistance=10k package=THT]
  R4 = Resistor [tolerance=±5% power=0.25 resistance=10k package=THT]

nets:
  N1: Part1.5V, J23.pin2
  N2: Q1.Gate, R1.Pin_0
  N3: Q1.drain, LED2.A
  N4: Q1.source, J1.terminal_11, R1.Pin_1
  N5: Q2.Gate, R2.Pin_0
  N6: Q2.drain, LED3.A
  N7: Q2.source, J28.terminal_5, R2.Pin_1
  N8: Q3.Gate, R3.Pin_0
  N9: Q3.drain, LED1.A
  N10: Q3.source, J1.terminal_10, R3.Pin_1
  N11: Q4.Gate, R4.Pin_0
  N12: Q4.drain, LED4.A
  N13: Q4.source, J28.terminal_4, R4.Pin_1
  N14: J1.terminal_1, J39.pin3
  N15: J1.terminal_2, J39.pin2
  N16: J1.terminal_3, J39.pin1
  N17: J1.terminal_4, J40.pin5
  N18: J1.terminal_5, M1.Pin_2, M1.Pin_4
  N19: J1.terminal_6, J7.terminal_2
  N20: M1.Pin_1, J22.terminal_2
  N21: M1.Pin_3, J41.terminal_1
  N22: J2.terminal_1, J22.terminal_3
  N23: J2.terminal_2, J28.terminal_11
  N24: J4.terminal_1, M4.pin_2
  N25: J4.terminal_2, M4.pin_1
  N26: J5.terminal_1, M5.pin_2
  N27: J5.terminal_2, M5.pin_1
  N28: J6.terminal_1, M3.pin_2
  N29: J6.terminal_2, M3.pin_1
  N30: J7.terminal_1, J22.terminal_4
  N31: J8.terminal_1, M2.pin_2
  N32: J8.terminal_2, M2.pin_1
  N33: LED1.C, J41.terminal_5
  N34: LED2.C, J41.terminal_4
  N35: LED3.C, J41.terminal_3
  N36: LED4.C, J41.terminal_2
  N37: J24.pin2, J32.pin5
  N38: J24.pin3, J31.pin5
  N39: J24.pin4, J29.pin5
  N40: J24.pin5, J19.pin5
  N41: J25.pin3, J38.pin5
  N42: J25.pin4, J37.pin5
  N43: J25.pin5, J35.pin5
  N44: J25.pin6, J34.pin5
  N45: J26.pin2, J38.pin4
  N46: J26.pin3, J37.pin4
  N47: J26.pin4, J35.pin4
  N48: J26.pin5, J34.pin4
  N49: J26.pin6, J23.pin6, J39.pin4, J40.pin6
  N50: J27.pin2, J32.terminal_4
  N51: J27.pin3, J31.terminal_4
  N52: J27.pin4, J29.terminal_4
  N53: J27.pin5, J19.terminal_4
  N54: J27.terminal_6, J23.terminal_7
  N55: J23.pin5, J21.pin5, J30.pin5, J33.pin5, J36.pin5
  N56: J21.pin4, J30.pin4, J33.pin4, J36.pin4

notes:
  + 12V
  + 5V
  encoder
  display
  -
  + 5v
  B
  A
  Din
  CS
  CLK
  - 0V (from 12V)
  L298N
